# Fritzing sketch smd_soldering_iron (saved by Fritzing 0.9.10b)
breadboards: 2

parts:
  U1 = attiny85 [package=dip]
  J1 = Generic male header - 4 pins [form="♂ (male)" package=THT]
  R1 = Temperature Sensor (Thermistor) [thermistor_type=NTC package=THT]  # not connected
  U2 = POT [knob_status=50% power=0.5W package=alps_pot]
  DB1 = DIAC Diode [part_number=DB3 package=DO-35]
  U3 = TRIAC [package=to-92]
  C3 = Capacitor [package=cap-pth-small2]
  C6 = Capacitor [package=cap-pth-small2]
  R2 = Resistor [tolerance=±5% resistance=10000 package="0603 [SMD]"]
  R3 = Resistor [tolerance=±5% resistance=270 package="0603 [SMD]"]

nets:
  N1: U1.Pin_4, J1.GND
  N2: U1.Pin_5, J1.SDA
  N3: U1.Pin_7, J1.SCL
  N4: U1.Pin_8, J1.VCC
  N5: U2.E, U3.G, R3.Pin_0
  N6: U2.S, U2.A, R2.Pin_0
  N7: DB1.Anode_1, C6.1, R2.Pin_1
  N8: DB1.Anode_2, U3.M2
  N9: U3.M1, C3.2, C6.2
  N10: C3.1, R3.Pin_1

notes:
  Input 220V AC
  220V AC -> 5V
  ( USB Charger )
  TC+ TC-
  MAX6675
  G V S C D
  Use any 220V AC dimmer DIY ( schematic from www.eleccircuit.com ), or just buy one and connect it to pink and green wires
  Heating plate
  Soldering Iron
  In A In B
  for SMD soldering with an
  Triac BT136:
  1- MT1
  2- MT2
  3- Gate
  I2C
  SPI
  ** Be careful if you try this **
  working with high voltage
  We are using an old hair iron as heating plate
  Soldering Iron heating plate
  ATTiny85, with K-type thermocouple using MAX6675, to see the temperature on the iron
  external temperature gauge
  Keep in mind that we are

custom parts:
  Generic male header - 4 pins: Generic male header
