# Fritzing sketch Arduino_Micro_Control_Audio_of_System_OS (saved by Fritzing 0.9.10b)
breadboards: 1

parts:
  Componente1 = Arduino Micro (Rev3)
  U1 = POT [knob_status=50% power=0.5W package=alps_pot]
  LED3 = LED - 5mm [color="Red (633nm)" current=0.030 package="5 mm [THT]"]
  R2 = Resistor [tolerance=±5% power=0.25 resistance=220 package=THT]

nets:
  N1: Componente1.D3/SCL, LED3.anode
  N2: Componente1.D6_PWM/A7, U1.S
  N3: Componente1.GND, U1.E, R2.Pin_1
  N4: Componente1.5V, U1.A
  N5: LED3.cathode, R2.Pin_0

notes:
  220 Ohm
