# Fritzing sketch ej1_pot_serv_LED_pantalla_serial (saved by Fritzing 0.9.9b)
breadboards: 1

parts:
  Componente1 = Arduino Nano (Rev3.0)
  J1 = Basic Servo
  R1 = Resistor [tolerance=±5% resistance=390 package="0603 [SMD]"]
  R2 = Rotary Potentiometer (Small) [maximum_resistance=100kΩ package=THT]
  R3 = Rotary Potentiometer (Small) [maximum_resistance=100kΩ package=THT]
  LED1 = smd LED [color="Red (633nm)" package="0805 [SMD]"]

nets:
  N1: Componente1.D2, R1.Pin_0
  N2: Componente1.D9, J1.pulse
  N3: Componente1.A1, R3.wiper
  N4: Componente1.A0, R2.wiper
  N5: J1.gnd, R2.leg1, R3.leg1
  N6: J1.vcc, R2.leg2, R3.leg2, LED1.anode
  N7: R1.Pin_1, LED1.cathode

notes:
  para el Servo
  para el LED
