# Fritzing sketch prac1-1_rele-btn1_enciende_btn2_apaga (saved by Fritzing 0.9.9b)
breadboards: 1

parts:
  Componente1 = Arduino Nano (Rev3.0)
  S5 = Pushbutton [package="[SMD]"]
  S6 = Pushbutton [package="[SMD]"]
  R1 = Resistor [tolerance=±5% resistance=10000 package="1206 [SMD]"]
  R2 = Resistor [tolerance=±5% resistance=10000 package="1206 [SMD]"]
  OMRON1 = OMRON PCB Power Relay – G5LE [part_number="G5LE-1\r\n" package=THT]
  M1 = DC Motor
  VCC1 = Battery

nets:
  N1: Componente1.D7, S6.Pin_3, S6.Pin_4, R1.Pin_1
  N2: Componente1.D8, S5.Pin_3, S5.Pin_4, R2.Pin_1
  N3: Componente1.D10, OMRON1.COIL1
  N4: S5.Pin_1, S5.Pin_2, S6.Pin_1, S6.Pin_2, OMRON1.C, VCC1.+
  N5: R1.Pin_0, R2.Pin_0, OMRON1.COIL2, M1.pin_1, VCC1.-
  N6: OMRON1.B, M1.pin_2

notes:
  Simula ser la entrada externa de 5V
  No tiene el modulo de relé, pero sí relés sueltos
