# Fritzing sketch prac1-2_rele_btn1_enciende_bombilla_230v (saved by Fritzing 0.9.9b)
breadboards: 1

parts:
  Componente1 = Arduino Nano (Rev3.0)
  S5 = Pushbutton [package="[SMD]"]
  R2 = Resistor [tolerance=±5% resistance=10000 package="1206 [SMD]"]
  OMRON1 = OMRON PCB Power Relay – G5LE [part_number="G5LE-1\r\n" package=THT]
  VCC1 = Battery
  VCC2 = Battery  # not connected
  LED1 = smd LED [color="Red (633nm)" package="1206 [SMD]"]  # not connected

nets:
  N1: Componente1.D8, S5.Pin_3, S5.Pin_4, R2.Pin_1
  N2: Componente1.D10, OMRON1.COIL1
  N3: S5.Pin_1, S5.Pin_2, OMRON1.COIL2, VCC1.-
  N4: R2.Pin_0, VCC1.+

notes:
  Simula ser la entrada externa de 5V
  No tiene el modulo de relé, pero sí relés sueltos
  Simula ser la entrada externa de 230v, y una bombilla de 230v AC
