# Fritzing sketch prac1-6_rele_sin_modulo_de_rele (saved by Fritzing 0.9.9b)
breadboards: 1

parts:
  Componente1 = Arduino Nano (Rev3.0)
  OMRON1 = OMRON PCB Power Relay – G5LE [part_number="G5LE-1\r\n" package=THT]
  VCC1 = Battery
  R1 = Resistor [tolerance=±5% power=0.25 resistance=220 package=THT]
  D1 = Rectifier Diode [part_number=1N4001 package="300 mil [THT]"]
  Q1 = NPN-Transistor [package="TO92 [THT]"]
  R2 = Resistor [tolerance=±5% power=0.25 resistance=1000 package=THT]
  LED1 = LED - 5mm [color="Red (633nm)" current=0.030 package="5 mm [THT]"]

nets:
  N1: Componente1.D9, R2.Pin_0
  N2: OMRON1.COIL1, D1.anode, Q1.C
  N3: OMRON1.C, R1.Pin_1
  N4: OMRON1.COIL2, VCC1.+, D1.cathode, LED1.anode
  N5: OMRON1.B, LED1.cathode
  N6: VCC1.-, R1.Pin_0, Q1.E
  N7: Q1.B, R2.Pin_1

notes:
  Simula ser la entrada externa de 5V
