# Fritzing sketch prac2_pwd_encender_LED_progresivamente (saved by Fritzing 0.9.9b)
breadboards: 1

parts:
  Componente2 = Arduino Nano (Rev3.0)
  LED1 = smd LED [color="Red (633nm)" package="1206 [SMD]"]
  R1 = Resistor [tolerance=±5% resistance=390 package="2010 [SMD]"]

nets:
  N1: Componente2.GND, LED1.cathode
  N2: Componente2.D9, R1.Pin_0
  N3: LED1.anode, R1.Pin_1
