# Fritzing sketch prac3_pwd_LED_con_potenciometro_0_1023_0_255 (saved by Fritzing 0.9.9b)
breadboards: 1

parts:
  Componente2 = Arduino Nano (Rev3.0)
  LED1 = smd LED [color="Red (633nm)" package="1206 [SMD]"]
  R1 = Resistor [tolerance=±5% resistance=390 package="2010 [SMD]"]
  U1 = POT [package=pot_alpha_rv16af-20]

nets:
  N1: Componente2.GND, LED1.cathode, U1.E
  N2: Componente2.D9, R1.Pin_0
  N3: Componente2.5V, U1.A
  N4: Componente2.A0, U1.S
  N5: LED1.anode, R1.Pin_1
