# Fritzing sketch prac4-1_servo_180_grados (saved by Fritzing 0.9.9b)
breadboards: 1

parts:
  Componente1 = Arduino Nano (Rev3.0)
  J1 = Basic Servo

nets:
  GND: Componente1.GND, J1.gnd
  N1: Componente1.D9, J1.pulse
  5V: Componente1.5V, J1.vcc
