# Fritzing sketch prac4-2_servo_con_potenciometro (saved by Fritzing 0.9.9b)
breadboards: 1

parts:
  Componente1 = Arduino Nano (Rev3.0)
  J1 = Basic Servo
  U1 = POT [package=pot_alpha_rv16af-20]

nets:
  GND: Componente1.GND, J1.gnd, U1.E
  N1: Componente1.D9, J1.pulse
  5V: Componente1.5V, J1.vcc, U1.A
  N2: Componente1.A0, U1.S
