# Fritzing sketch prac4-2_servo_potenciometro_pantalla (saved by Fritzing 0.9.9b)
breadboards: 1

parts:
  Componente1 = Arduino Nano (Rev3.0)
  J1 = Basic Servo
  U1 = POT [package=pot_alpha_rv16af-20]
  U2 = POT [package=pot_alpha_rv16af-20]
  LCD1 = LCD screen
  R1 = Resistor [tolerance=±5% resistance=390 package="0603 [SMD]"]

nets:
  GND: Componente1.GND, J1.gnd, U1.E, U2.E, LCD1.VSS, LCD1.R/W, LCD1.LED-
  N1: Componente1.D2, LCD1.DB7
  N2: Componente1.D3, LCD1.DB6
  N3: Componente1.D4, LCD1.DB5
  N4: Componente1.D5, LCD1.DB4
  N5: Componente1.D9, J1.pulse
  N6: Componente1.D11/MOSI, LCD1.E
  N7: Componente1.D12/MISO, LCD1.RS
  5V: Componente1.5V, J1.vcc, U1.A, U2.A, LCD1.VDD, R1.Pin_0
  N8: Componente1.A0, U1.S
  N9: U2.S, LCD1.V0
  N10: LCD1.LED+, R1.Pin_1
