# Fritzing sketch ej2_LED_Pot_pantalla (saved by Fritzing 0.9.9b)
breadboards: 1

parts:
  Componente1 = Arduino Nano (Rev3.0)
  R2 = Rotary Potentiometer (Small) [maximum_resistance=100kΩ package=THT]
  Grove1 = Grove OLED 128x96
  LED1 = smd LED [color="Red (633nm)" package="1206 [SMD]"]
  R3 = Resistor [tolerance=±5% power=0.25 resistance=390 package=THT]

nets:
  GND: Componente1.GND, R2.leg1, Grove1.GND
  N1: Componente1.D3, R3.Pin_0
  5V: Componente1.5V, R2.leg2, Grove1.VCC, LED1.anode
  N2: Componente1.A5, Grove1.SCL
  N3: Componente1.A4, Grove1.SDA
  N4: Componente1.A0, R2.wiper
  N5: LED1.cathode, R3.Pin_1
