# Fritzing sketch ej3_poten_servo_actua_tercios (saved by Fritzing 0.9.9b)
breadboards: 1

parts:
  Componente1 = Arduino Nano (Rev3.0)
  R2 = Rotary Potentiometer (Small) [maximum_resistance=100kΩ package=THT]
  J1 = Basic Servo

nets:
  GND: Componente1.GND, R2.leg1, J1.gnd
  N1: Componente1.D10, J1.pulse
  5V: Componente1.5V, R2.leg2, J1.vcc
  N2: Componente1.A0, R2.wiper
