# Fritzing sketch arduino_reloj_y_temperatura_mini_proyecto (saved by Fritzing 0.9.9b)
breadboards: 1

parts:
  Componente1 = Arduino Nano (Rev3.0)
  RHT1 = Humidity and Temperature Sensor RHT03
  Grove1 = Grove OLED 128x96
  ZS-042_RTC1 = ZS-042 RTC Module

nets:
  GND: Componente1.GND, RHT1.GND_2, Grove1.GND, ZS-042_RTC1.GND
  VCC: Componente1.5V, RHT1.Vcc, Grove1.VCC, ZS-042_RTC1.VCC
  N1: Componente1.A5, Grove1.SCL, ZS-042_RTC1.SCL
  N2: Componente1.A4, Grove1.SDA, ZS-042_RTC1.SDA
  N3: Componente1.A0, RHT1.Data-signal
