# Fritzing sketch 4-Pulsador_LED_2_boton (saved by Fritzing 0.9.9b)
breadboards: 1

parts:
  Componente1 = Arduino Nano (Rev3.0)
  R1 = Resistor [tolerance=±5% resistance=330 package="2512 [SMD]"]
  R2 = Resistor [tolerance=±5% resistance=10k package="2512 [SMD]"]
  LED1 = smd LED [color="Red (633nm)" package="0603 [SMD]"]
  S4 = Pushbutton [package="[THT]"]
  S5 = Pushbutton [package="[THT]"]
  R3 = Resistor [tolerance=±5% resistance=10k package="2512 [SMD]"]

nets:
  N1: Componente1.GND, R2.Pin_0, LED1.cathode, S5.Pin_1, S5.Pin_2
  N2: Componente1.D7, R2.Pin_1, S4.Pin_3, S4.Pin_4
  N3: Componente1.D9, S5.Pin_3, S5.Pin_4, R3.Pin_0
  N4: Componente1.D12/MISO, R1.Pin_1
  N5: Componente1.5V, S4.Pin_1, S4.Pin_2, R3.Pin_1
  N6: R1.Pin_0, LED1.anode
